# Fritzing sketch fritzingDiagramLab3 (saved by Fritzing 0.9.4)
breadboards: 1

parts:
  Part1 = Arduino Uno (Rev3)
  R1 = Resistor [tolerance=±5% resistance=220 package=THT]
  R2 = Resistor [tolerance=±5% resistance=220 package=THT]
  R3 = Resistor [tolerance=±5% resistance=220 package=THT]
  LED1 = LED - 5mm [color="Red (633nm)" package="5 mm [THT]"]
  LED2 = LED - 5mm [color="Green (560nm)" package="5 mm [THT]"]
  LED3 = LED - 5mm [color="Green (560nm)" package="5 mm [THT]"]
  R4 = Rotary Potentiometer (Small) [maximum_resistance=100kΩ package=THT]

nets:
  N1: Part1.A0, R4.wiper
  N2: Part1.D9_PWM, R3.Pin_1
  N3: Part1.D10_PWM/SS, R2.Pin_1
  N4: Part1.D11_PWM/MOSI, R1.Pin_1
  N5: Part1.GND, LED1.anode, LED2.anode, LED3.anode, R4.leg1
  N6: Part1.5V, R4.leg2
  N7: R1.Pin_0, LED2.cathode
  N8: R2.Pin_0, LED3.cathode
  N9: R3.Pin_0, LED1.cathode
